# Fritzing sketch PCB (saved by Fritzing 0.9.3b)
circuit board: 8.46667cm x 5.64444cm
breadboards: 1

parts:
  Part1 = BME280 Breakout
  part = Raspberry Pi 3 [part_number=RPI-3-V1.2]

nets:
  GND: Part1.GND, part.GND
  3V3: Part1.3.3V, part.3v3, part.3V3
  N1: Part1.SDI/SDA, part.GPIO2
  N2: Part1.SCK/SCL, part.GPIO3

notes:
  sda
  sci
  3.3v
  gnd
  sck
  sdo
  sdi
  !cs
